# Fritzing sketch ATmega328ProgrammerBoard (saved by Fritzing 0.9.4)
stripboards: 1

parts:
  Y1 = CRYSTAL [package=crystal-smd-10.5x4.8-2pin]
  C1 = Capacitor [package=cap-pth-5mm]
  C2 = Capacitor [package=cap-pth-5mm]
  J3 = female pin header, 10 pins [form="♀ (female)"]
  J4 = female pin header, 14 pins [form="♀ (female)"]
  J5 = female pin header, 14 pins [form="♀ (female)"]

nets:
  N1: Y1.1, C1.2, J5.pin9
  N2: Y1.2, C2.2, J5.pin10
  N3: C1.1, C2.1, J3.pin10, J5.pin8
  N4: J3.pin1, J4.pin3
  N5: J3.pin2, J5.pin7
  N6: J3.pin5, J5.pin1
  N7: J3.pin7, J4.pin5
  N8: J3.pin9, J4.pin4
